// Logisim project 21-Bit.circ as structural Verilog: 32 circuits, main circuit main
module main (
  input  [7:0] INPR,
  output [3:0] Seq
);

  wire ac_alu_controller_1_clr, ac_alu_controller_1_inc, ac_alu_controller_1_ld, ar_controler_1_clr,
       ar_controler_1_inr, ar_controler_1_ld, bus_controler_1_s0, bus_controler_1_s1, bus_controler_1_s2,
       CLK, dr_controller_1_inc, dr_controller_1_ld, E, E_out, FGI, FGO, I0, I1, IEN, ir_controller_1_ld,
       outr_controller_1_ld, pc_controller_1_clr, pc_controller_1_inc, pc_controller_1_ld, R,
       ram_controller_1_read, ram_controller_1_write, S, sc_controller_1_inc, sc_controller_1_ld,
       tr_controller_1_ld;
  wire [0:0] pc_1_bus_out_6;
  wire [3:0] pc_1_bus_out, pc_1_bus_out_3, pc_1_bus_out_4, pc_1_bus_out_5;
  wire [7:0] outr_1_bus_out;
  wire [7:4] pc_1_bus_out_2;
  wire [14:0] ar_1_bus_out;
  wire [15:0] Seq_t;
  wire [20:0] AC, alu_1_ac_input, bus_1_out_11, DR, IR, ram_1_data, TR;
  wire [20:15] ar_1_bus_out_2;

  Clock u_CLK (.out(CLK));
  Hex_Digit_Display hex_digit_display_1 (.value(INPR[7:4]));  // open: dp
  Hex_Digit_Display hex_digit_display_2 (.value(INPR[3:0]));  // open: dp
  R_Controller r_controller_1 (.Seq(Seq_t), .IEN(IEN), .FGI(FGI), .FGO(FGO), .Output(R), .CLK(CLK));
  I1_Controller i1_controller_1 (.IR(IR), .Seq(Seq_t), .out_5(I1), .R(R), .CLK(CLK));
  I0_Controller i0_controller_1 (.IR(IR), .Seq(Seq_t), .out_5(I0), .R(R), .CLK(CLK));
  S_Controller s_controller_1 (.IR(IR), .Seq(Seq_t), .Output(S), .CLK(CLK), .I0(I0), .I1(I1), .R(R));
  IEN_Controler ien_controler_1 (.IR(IR), .Seq(Seq_t), .I0(I0), .Output(IEN), .I1(I1), .CLK(CLK), .R(R));
  // FGI_Controller fgi_controller_1: pin names not known; wires that end beside it: Seq_t, IR, I0, I1, CLK, FGI
  FGO_Controller fgo_controller_1 (.IR(IR), .Seq(Seq_t), .Output(FGO), .CLK(CLK), .I0(I0), .I1(I1));
  SC_Controller sc_controller_1 (
    .IR(IR), .Seq(Seq_t), .I0(I0), .I1(I1), .R(R), .S(S), .LD(sc_controller_1_ld), .INC(sc_controller_1_inc));
  E_Controller e_controller_1 (
    .IR(IR), .AC(AC), .Seq(Seq_t), .R(R), .Output(E), .I0(I0), .I1(I1), .in_7(CLK), .Cout(E_out));
  Counter #(.width(4), .max('hf)) counter_1 (
    .load(sc_controller_1_ld), .D(4'b0000), .count(sc_controller_1_inc), .Q(Seq), .clk(CLK));  // open: carry, clr
  Decoder #(.select(4)) decoder_1 (
    .out0(Seq_t[0]), .out1(Seq_t[1]), .out2(Seq_t[2]), .out3(Seq_t[3]), .out4(Seq_t[4]), .out5(Seq_t[5]),
    .out6(Seq_t[6]), .out7(Seq_t[7]), .out8(Seq_t[8]), .out9(Seq_t[9]), .out10(Seq_t[10]), .out11(Seq_t[11]),
    .out12(Seq_t[12]), .out13(Seq_t[13]), .out14(Seq_t[14]), .out15(Seq_t[15]), .sel(Seq));  // open: en
  ALU alu_1 (
    .Seq(Seq_t), .IR(IR), .AC(AC), .DR(DR), .Carry_in(E), .I0(I0), .I1(I1), .C_out(E_out), .INPR(INPR),
    .AC_input(alu_1_ac_input), .TR(TR));
  OUTR_Controller outr_controller_1 (.IR(IR), .Seq(Seq_t), .LD(outr_controller_1_ld), .I1(I0), .I0(I1), .R(R));
  RAM #(.addrWidth(15), .dataWidth(21), .bus("separate")) ram_1 (
    .addr(ar_1_bus_out), .din(bus_1_out_11), .data(ram_1_data), .str(ram_controller_1_write), .clk(CLK),
    .ld(ram_controller_1_read));  // open: sel, clr
  RAM_Controller ram_controller_1 (
    .IR(IR), .Seq(Seq_t), .I0(I0), .Read(ram_controller_1_read), .I1(I1), .R(R),
    .Write(ram_controller_1_write));
  AR_Controler ar_controler_1 (
    .IR(IR), .Seq(Seq_t), .LD(ar_controler_1_ld), .I0(I0), .I1(I1), .R(R), .INR(ar_controler_1_inr),
    .CLR(ar_controler_1_clr));
  PC_Controller pc_controller_1 (
    .IR(IR), .Seq(Seq_t), .I0(I0), .I1(I1), .LD(pc_controller_1_ld), .R(R), .E(E), .FGI(FGI), .FGO(FGO),
    .INC(pc_controller_1_inc), .CLR(pc_controller_1_clr), .AC(AC), .DR(DR));
  DR_Controller dr_controller_1 (
    .IR(IR), .Seq(Seq_t), .I0(I0), .I1(I1), .R(R), .LD(dr_controller_1_ld), .INC(dr_controller_1_inc));
  IR_Controller ir_controller_1 (.IR(IR), .Seq(Seq_t), .LD(ir_controller_1_ld), .R(R));
  TR_Controller tr_controller_1 (.IR(IR), .Seq(Seq_t), .LD(tr_controller_1_ld), .R(R));
  BUS_Controler bus_controler_1 (
    .IR(IR), .R(R), .I0(I0), .S0(bus_controler_1_s0), .S1(bus_controler_1_s1), .S2(bus_controler_1_s2),
    .Seq(Seq_t), .I1(I1));
  // Probe on ram_1_data
  AR ar_1 (
    .Bus_IN(bus_1_out_11), .Bus_OUT({ar_1_bus_out_2, ar_1_bus_out}), .Inc(ar_controler_1_inr),
    .Load(ar_controler_1_ld), .Clock(CLK), .Clear(ar_controler_1_clr));
  PC pc_1 (
    .Bus_OUT({pc_1_bus_out_6[0], pc_1_bus_out_5, pc_1_bus_out_4, pc_1_bus_out_3, pc_1_bus_out_2, pc_1_bus_out}),
    .Bus_IN(bus_1_out_11), .Inc(pc_controller_1_inc), .Load(pc_controller_1_ld), .Clock(CLK),
    .Clear(pc_controller_1_clr));
  DR dr_1 (
    .ALU_In(bus_1_out_11), .Bus_OUT(DR), .Load(dr_controller_1_ld), .Inc(dr_controller_1_inc), .Clock(CLK));  // open: Clear
  AC ac_1 (
    .ALU_In(alu_1_ac_input), .Bus_OUT(AC), .Inc(ac_alu_controller_1_inc), .Load(ac_alu_controller_1_ld),
    .Clock(CLK), .Clear(ac_alu_controller_1_clr));
  AC_ALU_Controller ac_alu_controller_1 (
    .IR(IR), .Seq(Seq_t), .I0(I0), .I1(I1), .INC(ac_alu_controller_1_inc), .LD(ac_alu_controller_1_ld),
    .CLR(ac_alu_controller_1_clr));
  IR ir_1 (.BUS_IN(bus_1_out_11), .Bus_OUT(IR), .Load(ir_controller_1_ld), .Clock(CLK));
  TR tr_1 (.ALU_In(bus_1_out_11), .Bus_OUT(TR), .Load(tr_controller_1_ld), .Clock(CLK));  // open: Clear
  OUTR outr_1 (.ALU_In(bus_1_out_11), .Bus_OUT(outr_1_bus_out), .Load(outr_controller_1_ld), .Clock(CLK));
  Hex_Digit_Display hex_digit_display_3 (.value({3'b000, ar_1_bus_out_2[20]}));  // open: dp
  // Probe on {ar_1_bus_out_2, ar_1_bus_out}
  // Probe on {pc_1_bus_out_6[0], pc_1_bus_out_5, pc_1_bus_out_4, pc_1_bus_out_3, pc_1_bus_out_2, pc_1_bus_out}
  // Probe on DR
  // Probe on AC
  // Probe on IR
  // Probe on TR
  // Probe on outr_1_bus_out
  Hex_Digit_Display hex_digit_display_4 (.value(ar_1_bus_out_2[19:16]));  // open: dp
  Hex_Digit_Display hex_digit_display_5 (.value({ar_1_bus_out_2[15], ar_1_bus_out[14:12]}));  // open: dp
  Hex_Digit_Display hex_digit_display_6 (.value({3'b000, pc_1_bus_out_6[0]}));  // open: dp
  Hex_Digit_Display hex_digit_display_7 (.value(pc_1_bus_out_5));  // open: dp
  Hex_Digit_Display hex_digit_display_8 (.value(DR[19:16]));  // open: dp
  Hex_Digit_Display hex_digit_display_9 (.value({3'b000, DR[20]}));  // open: dp
  Hex_Digit_Display hex_digit_display_10 (.value({3'b000, AC[20]}));  // open: dp
  Hex_Digit_Display hex_digit_display_11 (.value(AC[19:16]));  // open: dp
  Hex_Digit_Display hex_digit_display_12 (.value(IR[19:16]));  // open: dp
  Hex_Digit_Display hex_digit_display_13 (.value({3'b000, IR[20]}));  // open: dp
  Hex_Digit_Display hex_digit_display_14 (.value(TR[19:16]));  // open: dp
  Hex_Digit_Display hex_digit_display_15 (.value({3'b000, TR[20]}));  // open: dp
  Hex_Digit_Display hex_digit_display_16 (.value(ar_1_bus_out[7:4]));  // open: dp
  Hex_Digit_Display hex_digit_display_17 (.value(ar_1_bus_out[11:8]));  // open: dp
  Hex_Digit_Display hex_digit_display_18 (.value(pc_1_bus_out_4));  // open: dp
  Hex_Digit_Display hex_digit_display_19 (.value(pc_1_bus_out_3));  // open: dp
  Hex_Digit_Display hex_digit_display_20 (.value(DR[15:12]));  // open: dp
  Hex_Digit_Display hex_digit_display_21 (.value(DR[11:8]));  // open: dp
  Hex_Digit_Display hex_digit_display_22 (.value(AC[11:8]));  // open: dp
  Hex_Digit_Display hex_digit_display_23 (.value(AC[15:12]));  // open: dp
  Hex_Digit_Display hex_digit_display_24 (.value(IR[11:8]));  // open: dp
  Hex_Digit_Display hex_digit_display_25 (.value(IR[15:12]));  // open: dp
  Hex_Digit_Display hex_digit_display_26 (.value(TR[15:12]));  // open: dp
  Hex_Digit_Display hex_digit_display_27 (.value(TR[11:8]));  // open: dp
  Hex_Digit_Display hex_digit_display_28 (.value(outr_1_bus_out[7:4]));  // open: dp
  Hex_Digit_Display hex_digit_display_29 (.value(ar_1_bus_out[3:0]));  // open: dp
  Hex_Digit_Display hex_digit_display_30 (.value(pc_1_bus_out));  // open: dp
  Hex_Digit_Display hex_digit_display_31 (.value(pc_1_bus_out_2));  // open: dp
  Hex_Digit_Display hex_digit_display_32 (.value(DR[7:4]));  // open: dp
  Hex_Digit_Display hex_digit_display_33 (.value(DR[3:0]));  // open: dp
  Hex_Digit_Display hex_digit_display_34 (.value(AC[3:0]));  // open: dp
  Hex_Digit_Display hex_digit_display_35 (.value(AC[7:4]));  // open: dp
  Hex_Digit_Display hex_digit_display_36 (.value(IR[7:4]));  // open: dp
  Hex_Digit_Display hex_digit_display_37 (.value(IR[3:0]));  // open: dp
  Hex_Digit_Display hex_digit_display_38 (.value(TR[7:4]));  // open: dp
  Hex_Digit_Display hex_digit_display_39 (.value(TR[3:0]));  // open: dp
  Hex_Digit_Display hex_digit_display_40 (.value(outr_1_bus_out[3:0]));  // open: dp
  BUS bus_1 (
    .S0(bus_controler_1_s0), .S1(bus_controler_1_s1), .S2(bus_controler_1_s2),
    .AR({ar_1_bus_out_2, ar_1_bus_out}),
    .PC({pc_1_bus_out_6[0], pc_1_bus_out_5, pc_1_bus_out_4, pc_1_bus_out_3, pc_1_bus_out_2, pc_1_bus_out}),
    .DR(DR), .AC(AC), .IR(IR), .TR(TR), .RAM(ram_1_data), .out_11(bus_1_out_11));
  // Probe on bus_1_out_11
  Hex_Digit_Display hex_digit_display_41 (.value(Seq));  // open: dp
  Hex_Digit_Display hex_digit_display_42 (.value({3'b000, I0}));  // open: dp
  Hex_Digit_Display hex_digit_display_43 (.value({3'b000, I1}));  // open: dp

  // Other names for the same wires on the sheet: Seq1[3:0] = Seq

  // Notes on the sheet:
  //   NPR BASIC COMPUTER
  //   NPR BASIC COMPUTER
  //   T
  //   I0
  //   I1
endmodule

module BUS (
  input  S0,
  input  S1,
  input  S2,
  input  [20:0] AR,
  input  [20:0] PC,
  input  [20:0] DR,
  input  [20:0] AC,
  input  [20:0] IR,
  input  [20:0] TR,
  input  [20:0] RAM,
  output [20:0] out_11
);

  Multiplexer #(.select(3), .width(21)) multiplexer_1 (
    .in1(AR), .in2(PC), .in3(DR), .in4(AC), .in5(IR), .in6(TR), .in7(RAM), .out(out_11), .sel({S2, S1, S0}));  // open: in0, en

  // Other names for the same wires on the sheet: Selector[2:0] = {S2, S1, S0}
endmodule

module BUS_Controler (
  input  [20:0] IR,
  input  [15:0] Seq,
  input  R,
  input  I0,
  input  I1,
  output S0,
  output S1,
  output S2
);

  wire and_1_out, and_2_out, and_3_out, and_4_out, and_5_out, and_6_out, and_7_out, and_8_out, and_9_out,
       and_10_out, and_11_out, and_12_out, and_13_out, and_14_out, and_15_out, and_16_out, and_17_out,
       and_18_out, and_19_out, and_20_out, and_21_out, and_22_out, and_23_out, and_24_out, decoder_1_out0,
       decoder_1_out1, decoder_1_out2, decoder_1_out3, decoder_1_out4, decoder_1_out5, decoder_1_out6,
       decoder_1_out7, decoder_1_out8, decoder_1_out9, decoder_1_out10, decoder_1_out11, decoder_1_out12,
       decoder_1_out13, decoder_1_out14, decoder_1_out15, or_1_out, or_2_out, or_3_out, or_4_out, or_5_out,
       or_6_out;

  Decoder #(.select(4)) decoder_1 (
    .out0(decoder_1_out0), .out1(decoder_1_out1), .out2(decoder_1_out2), .out3(decoder_1_out3),
    .out4(decoder_1_out4), .out5(decoder_1_out5), .out6(decoder_1_out6), .out7(decoder_1_out7),
    .out8(decoder_1_out8), .out9(decoder_1_out9), .out10(decoder_1_out10), .out11(decoder_1_out11),
    .out12(decoder_1_out12), .out13(decoder_1_out13), .out14(decoder_1_out14), .out15(decoder_1_out15),
    .sel(IR[18:15]));  // open: en
  and and_1 (and_1_out, decoder_1_out15, Seq[3], I0, I1);
  and and_2 (and_2_out, decoder_1_out13, IR[20]);
  and and_3 (and_3_out, Seq[5], decoder_1_out4);
  and and_4 (and_4_out, ~decoder_1_out15, Seq[3], I0, ~I1);  // AND_Gate
  and and_5 (and_5_out, ~R, Seq[0]);  // AND_Gate
  and and_6 (and_6_out, R, Seq[0]);
  and and_7 (and_7_out, decoder_1_out13, Seq[5]);
  and and_8 (and_8_out, decoder_1_out11, Seq[5]);
  and and_9 (and_9_out, decoder_1_out8, IR[20]);
  and and_10 (and_10_out, decoder_1_out3, IR[20]);
  and and_11 (and_11_out, decoder_1_out5, IR[20]);
  and and_12 (and_12_out, decoder_1_out2, Seq[5]);
  and and_13 (and_13_out, decoder_1_out7, Seq[5]);
  and and_14 (and_14_out, decoder_1_out8, Seq[5]);
  and and_15 (and_15_out, IR[6], and_1_out);
  and and_16 (and_16_out, Seq[2], ~R);  // AND_Gate
  and and_17 (and_17_out, R, Seq[1]);
  and and_18 (and_18_out, decoder_1_out2, IR[20]);
  and and_19 (and_19_out, decoder_1_out8, Seq[7]);
  and and_20 (and_20_out, ~R, Seq[1]);  // AND_Gate
  and and_21 (and_21_out, ~decoder_1_out15, ~I0, ~I1, Seq[3]);  // AND_Gate
  and and_22 (and_22_out, ~decoder_1_out15, ~I0, I1, Seq[3]);  // AND_Gate
  and and_23 (and_23_out, ~decoder_1_out15, ~I0, I1, Seq[4]);  // AND_Gate
  or or_1 (or_1_out, and_2_out, and_4_out, and_3_out);
  or or_2 (or_2_out, and_5_out, and_6_out, and_7_out);
  or or_3 (or_3_out, and_8_out, and_9_out, and_10_out, and_11_out);
  or or_4 (or_4_out, and_12_out, and_13_out, and_14_out, and_15_out);
  or or_5 (or_5_out, and_17_out, and_18_out, and_19_out);
  or or_6 (or_6_out, and_20_out, and_21_out, and_22_out, and_23_out);
  and and_24 (and_24_out, ~or_6_out, ~or_5_out, ~and_16_out, ~or_4_out, ~or_3_out, ~or_2_out, ~or_1_out);  // AND_Gate
  Priority_Encoder priority_encoder_1 (
    .in0(and_24_out), .in1(or_1_out), .in2(or_2_out), .in3(or_3_out), .in4(or_4_out), .in5(and_16_out),
    .in6(or_5_out), .in7(or_6_out), .out({S2, S1, S0}));  // open: en_in, gs, en_out

  assign Seq[6] = IR[20];
endmodule

module AR (
  input  [20:0] Bus_IN,
  input  Load,
  input  Inc,
  input  Clear,
  input  Clock,
  output [20:0] Bus_OUT
);

  Counter #(.width(15), .max('h7fff)) counter_1 (
    .load(Load), .D(Bus_IN[14:0]), .count(Inc), .Q(Bus_OUT[14:0]), .clk(Clock), .clr(Clear));  // open: carry

  assign Bus_OUT[20:15] = {6{1'b0}};
endmodule

module PC (
  input  [20:0] Bus_IN,
  input  Load,
  input  Inc,
  input  Clear,
  input  Clock,
  output [20:0] Bus_OUT
);

  Counter #(.width(15), .max('h7fff)) counter_1 (
    .load(Load), .D(Bus_IN[14:0]), .count(Inc), .Q(Bus_OUT[14:0]), .clk(Clock), .clr(Clear));  // open: carry

  assign Bus_OUT[20:15] = {6{1'b0}};
endmodule

module DR (
  input  [20:0] ALU_In,
  input  Load,
  input  Inc,
  input  Clear,
  input  Clock,
  output [20:0] Bus_OUT
);

  Counter #(.width(21), .max('h1fffff)) counter_1 (
    .load(Load), .D(ALU_In), .count(Inc), .Q(Bus_OUT), .clk(Clock), .clr(Clear));  // open: carry
endmodule

module AC (
  input  [20:0] ALU_In,
  input  Load,
  input  Inc,
  input  Clock,
  input  Clear,
  output [20:0] Bus_OUT
);

  Counter #(.width(21), .max('h1fffff)) counter_1 (
    .load(Load), .D(ALU_In), .count(Inc), .Q(Bus_OUT), .clk(Clock), .clr(Clear));  // open: carry
endmodule

module IR (
  input  [20:0] BUS_IN,
  input  Load,
  input  Clock,
  output [20:0] Bus_OUT
);

  Counter #(.width(21), .max('h1fffff)) counter_1 (
    .load(Load), .D(BUS_IN), .count(1'b0), .Q(Bus_OUT), .clk(Clock), .clr(1'b0));  // open: carry
endmodule

module TR (
  input  [20:0] ALU_In,
  input  Load,
  input  Clear,
  input  Clock,
  output [20:0] Bus_OUT
);

  Counter #(.width(21), .max('h1fffff)) counter_1 (
    .load(Load), .D(ALU_In), .count(1'b0), .Q(Bus_OUT), .clk(Clock), .clr(Clear));  // open: carry
endmodule

module OUTR (
  input  [20:0] ALU_In,
  input  Load,
  input  Clock,
  output [7:0] Bus_OUT
);

  Counter counter_1 (.load(Load), .D(ALU_In[7:0]), .count(1'b0), .Q(Bus_OUT), .clk(Clock));  // open: carry, clr
endmodule

module FA (
  input  Cin,
  input  A,
  input  B,
  output S,
  output Cout
);

  wire and_1_out, and_2_out, xor_1_out;

  xor xor_1 (xor_1_out, A, B);
  and and_1 (and_1_out, A, B);
  xor xor_2 (S, xor_1_out, Cin);
  and and_2 (and_2_out, xor_1_out, Cin);
  or or_1 (Cout, and_2_out, and_1_out);
endmodule

module RAM_Controller (
  input  [20:0] IR,
  input  [15:0] Seq,
  input  I0,
  input  I1,
  input  R,
  output Read,
  output Write
);

  wire and_1_out, and_2_out, and_3_out, and_4_out, and_5_out, and_6_out, and_7_out, and_8_out, and_9_out,
       decoder_1_out0, decoder_1_out1, decoder_1_out2, decoder_1_out3, decoder_1_out4, decoder_1_out5,
       decoder_1_out6, decoder_1_out7, decoder_1_out8, decoder_1_out9, decoder_1_out10, decoder_1_out11,
       decoder_1_out12, decoder_1_out13, decoder_1_out14, decoder_1_out15;

  Decoder #(.select(4)) decoder_1 (
    .out0(decoder_1_out0), .out1(decoder_1_out1), .out2(decoder_1_out2), .out3(decoder_1_out3),
    .out4(decoder_1_out4), .out5(decoder_1_out5), .out6(decoder_1_out6), .out7(decoder_1_out7),
    .out8(decoder_1_out8), .out9(decoder_1_out9), .out10(decoder_1_out10), .out11(decoder_1_out11),
    .out12(decoder_1_out12), .out13(decoder_1_out13), .out14(decoder_1_out14), .out15(decoder_1_out15),
    .sel(IR[18:15]));  // open: en
  and and_1 (and_1_out, R, Seq[1]);
  and and_2 (and_2_out, decoder_1_out7, Seq[5]);
  and and_3 (and_3_out, decoder_1_out13, Seq[5]);
  and and_4 (and_4_out, decoder_1_out10, Seq[6]);
  and and_5 (and_5_out, decoder_1_out12, Seq[6]);
  and and_6 (and_6_out, ~R, Seq[1]);  // AND_Gate
  and and_7 (and_7_out, ~decoder_1_out15, ~I1, ~I0, Seq[3]);  // AND_Gate
  and and_8 (and_8_out, I1, ~decoder_1_out15, ~I0, Seq[3]);  // AND_Gate
  and and_9 (and_9_out, ~decoder_1_out15, ~I0, I1, Seq[4]);  // AND_Gate
  or or_1 (Read, and_6_out, and_7_out, and_8_out, and_9_out);
  or or_2 (Write, and_1_out, and_2_out, and_3_out, and_4_out, and_5_out);
endmodule

module AR_Controler (
  input  [20:0] IR,
  input  [15:0] Seq,
  input  I0,
  input  I1,
  input  R,
  output LD,
  output INR,
  output CLR
);

  wire and_1_out, and_2_out, and_3_out, decoder_1_out0, decoder_1_out1, decoder_1_out2, decoder_1_out3,
       decoder_1_out4, decoder_1_out5, decoder_1_out6, decoder_1_out7, decoder_1_out8, decoder_1_out9,
       decoder_1_out10, decoder_1_out11, decoder_1_out12, decoder_1_out13, decoder_1_out14, decoder_1_out15;

  Decoder #(.select(4)) decoder_1 (
    .out0(decoder_1_out0), .out1(decoder_1_out1), .out2(decoder_1_out2), .out3(decoder_1_out3),
    .out4(decoder_1_out4), .out5(decoder_1_out5), .out6(decoder_1_out6), .out7(decoder_1_out7),
    .out8(decoder_1_out8), .out9(decoder_1_out9), .out10(decoder_1_out10), .out11(decoder_1_out11),
    .out12(decoder_1_out12), .out13(decoder_1_out13), .out14(decoder_1_out14), .out15(decoder_1_out15),
    .sel(IR[18:15]));  // open: en
  and and_1 (and_1_out, ~decoder_1_out15, I1, ~I0, Seq[3]);  // AND_Gate
  and and_2 (and_2_out, Seq[0], ~R);  // AND_Gate
  and and_3 (and_3_out, ~R, Seq[2]);  // AND_Gate
  and and_4 (INR, decoder_1_out13, Seq[5]);
  and and_5 (CLR, Seq[0], R);
  or or_1 (LD, and_1_out, and_2_out, and_3_out);
endmodule

module PC_Controller (
  input  [20:0] IR,
  input  [15:0] Seq,
  input  I0,
  input  I1,
  input  R,
  input  E,
  input  FGI,
  input  FGO,
  input  [20:0] AC,
  input  [20:0] DR,
  output LD,
  output INC,
  output CLR
);

  wire AC_t, and_3_out, and_4_out, and_5_out, and_6_out, and_7_out, and_8_out, and_9_out, and_10_out,
       and_11_out, and_12_out, and_13_out, and_14_out, and_15_out, and_16_out, and_17_out, decoder_1_out0,
       decoder_1_out1, decoder_1_out2, decoder_1_out3, decoder_1_out4, decoder_1_out5, decoder_1_out6,
       decoder_1_out7, decoder_1_out8, decoder_1_out9, decoder_1_out10, decoder_1_out11, decoder_1_out12,
       decoder_1_out13, decoder_1_out14, decoder_1_out15, DR_t, p, r_t;

  or or_1 (AC_t, AC[0], AC[1], AC[2], AC[3], AC[4], AC[5], AC[6], AC[7], AC[8], AC[9], AC[10], AC[11], AC[12], AC[13], AC[14], AC[15], AC[16], AC[17], AC[18], AC[19], AC[20]);
  or or_2 (DR_t, DR[0], DR[1], DR[2], DR[3], DR[4], DR[5], DR[6], DR[7], DR[8], DR[9], DR[10], DR[11], DR[12], DR[13], DR[14], DR[15], DR[16], DR[17], DR[18], DR[19], DR[20]);
  Decoder #(.select(4)) decoder_1 (
    .out0(decoder_1_out0), .out1(decoder_1_out1), .out2(decoder_1_out2), .out3(decoder_1_out3),
    .out4(decoder_1_out4), .out5(decoder_1_out5), .out6(decoder_1_out6), .out7(decoder_1_out7),
    .out8(decoder_1_out8), .out9(decoder_1_out9), .out10(decoder_1_out10), .out11(decoder_1_out11),
    .out12(decoder_1_out12), .out13(decoder_1_out13), .out14(decoder_1_out14), .out15(decoder_1_out15),
    .sel(IR[18:15]));  // open: en
  and and_1 (r_t, decoder_1_out15, ~I1, ~I0, IR[20]);  // AND_Gate
  and and_2 (p, decoder_1_out15, I1, I0, IR[20]);
  and and_3 (and_3_out, decoder_1_out4, Seq[5]);
  and and_4 (and_4_out, decoder_1_out13, Seq[6]);
  and and_5 (and_5_out, ~R, Seq[1]);  // AND_Gate
  and and_6 (and_6_out, R, Seq[2]);
  and and_7 (and_7_out, decoder_1_out2, ~AC_t, Seq[6]);  // AND_Gate
  and and_8 (and_8_out, decoder_1_out3, ~DR_t, Seq[6]);  // AND_Gate
  and and_9 (and_9_out, decoder_1_out5, ~DR_t, Seq[6]);  // AND_Gate
  and and_10 (and_10_out, r_t, ~AC[20], IR[2]);  // AND_Gate
  and and_11 (and_11_out, r_t, AC[20], IR[4]);
  and and_12 (and_12_out, r_t, ~AC_t, IR[8]);  // AND_Gate
  and and_13 (and_13_out, r_t, ~E, IR[13]);  // AND_Gate
  and and_14 (and_14_out, p, FGI, IR[1]);
  and and_15 (and_15_out, p, ~FGI, IR[2]);  // AND_Gate
  and and_16 (and_16_out, p, FGO, IR[3]);
  and and_17 (and_17_out, p, ~FGO, IR[7]);  // AND_Gate
  and and_18 (CLR, R, Seq[1]);
  or or_3 (LD, and_3_out, and_4_out);
  or or_4 (INC, and_5_out, and_6_out, and_7_out, and_8_out, and_9_out, and_10_out, and_11_out, and_12_out, and_13_out, and_14_out, and_15_out, and_16_out, and_17_out);

  assign Seq[3] = IR[20];

  // Other names for the same wires on the sheet: AC_20 = AC[20]
endmodule

module DR_Controller (
  input  [20:0] IR,
  input  [15:0] Seq,
  input  I0,
  input  I1,
  input  R,
  output LD,
  output INC
);

  wire and_1_out, and_2_out, and_3_out, and_4_out, and_5_out, and_6_out, and_7_out, decoder_1_out0,
       decoder_1_out1, decoder_1_out2, decoder_1_out3, decoder_1_out4, decoder_1_out5, decoder_1_out6,
       decoder_1_out7, decoder_1_out8, decoder_1_out9, decoder_1_out10, decoder_1_out11, decoder_1_out12,
       decoder_1_out13, decoder_1_out14, decoder_1_out15;

  Decoder #(.select(4)) decoder_1 (
    .out0(decoder_1_out0), .out1(decoder_1_out1), .out2(decoder_1_out2), .out3(decoder_1_out3),
    .out4(decoder_1_out4), .out5(decoder_1_out5), .out6(decoder_1_out6), .out7(decoder_1_out7),
    .out8(decoder_1_out8), .out9(decoder_1_out9), .out10(decoder_1_out10), .out11(decoder_1_out11),
    .out12(decoder_1_out12), .out13(decoder_1_out13), .out14(decoder_1_out14), .out15(decoder_1_out15),
    .sel(IR[18:15]));  // open: en
  and and_1 (and_1_out, decoder_1_out8, Seq[7]);
  and and_2 (and_2_out, decoder_1_out12, Seq[5]);
  and and_3 (and_3_out, Seq[3], ~decoder_1_out15, ~I0, ~I1);  // AND_Gate
  and and_4 (and_4_out, Seq[4], ~decoder_1_out15, ~I0, I1);  // AND_Gate
  and and_5 (and_5_out, Seq[3], ~decoder_1_out15, I0, ~I1);  // AND_Gate
  and and_6 (and_6_out, decoder_1_out3, Seq[5]);
  and and_7 (and_7_out, decoder_1_out5, Seq[5]);
  or or_1 (INC, and_6_out, and_7_out);
  or or_2 (LD, and_1_out, and_2_out, and_3_out, and_4_out, and_5_out);
endmodule

module AC_Controller (
  input  [20:0] IR,
  input  [15:0] Seq,
  input  I0,
  input  I1,
  input  R,
  output LD,
  output INC,
  output CLR
);

  wire ADD_out, AND_out, COM_out, decoder_1_out8, decoder_1_out9, decoder_1_out10, decoder_1_out11,
       decoder_1_out12, decoder_1_out13, decoder_1_out14, decoder_1_out15, DR_out, INPR_out, p_out, SHL_out,
       SHR_out;
  wire [7:0] decoder_1_out7;

  Decoder #(.select(4)) decoder_1 (
    .out0(decoder_1_out7[7]), .out1(decoder_1_out7[6]), .out2(decoder_1_out7[5]), .out3(decoder_1_out7[4]),
    .out4(decoder_1_out7[3]), .out5(decoder_1_out7[2]), .out6(decoder_1_out7[1]), .out7(decoder_1_out7[0]),
    .out8(decoder_1_out8), .out9(decoder_1_out9), .out10(decoder_1_out10), .out11(decoder_1_out11),
    .out12(decoder_1_out12), .out13(decoder_1_out13), .out14(decoder_1_out14), .out15(decoder_1_out15),
    .sel(IR[17:14]));  // open: en
  and p (p_out, decoder_1_out15, I0, I1, Seq[3]);
  and AND (AND_out, decoder_1_out7[7], Seq[5]);
  and ADD (ADD_out, decoder_1_out7[2], Seq[5]);
  and DR (DR_out, decoder_1_out8, Seq[5]);
  and INPR (INPR_out, p_out, IR[13]);
  and COM (COM_out, R, IR[9]);
  and SHR (SHR_out, R, IR[7]);
  and SHL (SHL_out, R, IR[6]);
  and u_INC (INC, R, IR[5]);
  and u_CLR (CLR, R, IR[11]);
  or or_1 (LD, AND_out, ADD_out, DR_out, INPR_out, COM_out, SHR_out, SHL_out);
endmodule

module AC_ALU_Controller (
  input  [20:0] IR,
  input  [15:0] Seq,
  input  I0,
  input  I1,
  output INC,
  output LD,
  output CLR
);

  wire ADD_out, AND_2_out, COM_out, DEC_out, decoder_1_out0, decoder_1_out1, decoder_1_out2, decoder_1_out3,
       decoder_1_out4, decoder_1_out5, decoder_1_out6, decoder_1_out7, decoder_1_out8, decoder_1_out9,
       decoder_1_out10, decoder_1_out11, decoder_1_out12, decoder_1_out13, decoder_1_out14, decoder_1_out15,
       DR_2_out, DR_out, INPR_out, NAND_out, NOR_out, or_2_out, or_3_out, OR_out, p_out, r, SHL_out, SHR_out,
       SUB_out, TR_out, XOR_2_out, XOR_out;

  Decoder #(.select(4)) decoder_1 (
    .out0(decoder_1_out0), .out1(decoder_1_out1), .out2(decoder_1_out2), .out3(decoder_1_out3),
    .out4(decoder_1_out4), .out5(decoder_1_out5), .out6(decoder_1_out6), .out7(decoder_1_out7),
    .out8(decoder_1_out8), .out9(decoder_1_out9), .out10(decoder_1_out10), .out11(decoder_1_out11),
    .out12(decoder_1_out12), .out13(decoder_1_out13), .out14(decoder_1_out14), .out15(decoder_1_out15),
    .sel(IR[18:15]));  // open: en
  and p (p_out, decoder_1_out15, I0, I1, Seq[3]);
  and and_1 (r, decoder_1_out15, ~I1, ~I0, Seq[3]);  // AND_Gate
  and AND_2 (AND_2_out, decoder_1_out0, Seq[5]);
  and ADD (ADD_out, decoder_1_out12, Seq[5]);
  and DR (DR_out, decoder_1_out8, Seq[6]);
  and DR_2 (DR_2_out, decoder_1_out11, Seq[5]);
  and INPR (INPR_out, p_out, IR[12]);
  and COM (COM_out, r, IR[6]);
  and SHR (SHR_out, r, IR[7]);
  and SHL (SHL_out, r, IR[10]);
  and u_INC (INC, r, IR[5]);
  and u_CLR (CLR, r, IR[12]);
  and OR (OR_out, decoder_1_out0, Seq[5]);
  and XOR (XOR_out, decoder_1_out2, Seq[5]);
  and XOR_2 (XOR_2_out, decoder_1_out6, Seq[5]);
  and NAND (NAND_out, decoder_1_out10, Seq[5]);
  and NOR (NOR_out, decoder_1_out9, Seq[5]);
  and SUB (SUB_out, decoder_1_out14, Seq[5]);
  and TR (TR_out, decoder_1_out2, Seq[6]);
  and DEC (DEC_out, r, IR[3]);
  or or_2 (or_2_out, DR_out, DR_2_out);
  or or_3 (or_3_out, XOR_out, XOR_2_out);
  or or_4 (LD, AND_2_out, ADD_out, or_2_out, INPR_out, COM_out, SHR_out, SHL_out, OR_out, or_3_out, NAND_out, NOR_out, SUB_out, TR_out, DEC_out);
endmodule

module IR_Controller (
  input  [20:0] IR,
  input  [15:0] Seq,
  input  R,
  output LD
);

  wire decoder_1_out0, decoder_1_out1, decoder_1_out2, decoder_1_out3, decoder_1_out4, decoder_1_out5,
       decoder_1_out6, decoder_1_out7, decoder_1_out8, decoder_1_out9, decoder_1_out10, decoder_1_out11,
       decoder_1_out12, decoder_1_out13, decoder_1_out14;

  Decoder #(.select(4)) decoder_1 (
    .out0(decoder_1_out0), .out1(decoder_1_out1), .out2(decoder_1_out2), .out3(decoder_1_out3),
    .out4(decoder_1_out4), .out5(decoder_1_out5), .out6(decoder_1_out6), .out7(decoder_1_out7),
    .out8(decoder_1_out8), .out9(decoder_1_out9), .out10(decoder_1_out10), .out11(decoder_1_out11),
    .out12(decoder_1_out12), .out13(decoder_1_out13), .out14(decoder_1_out14), .sel(IR[18:15]));  // open: out15, en
  and and_1 (LD, ~R, Seq[1]);  // AND_Gate
endmodule

module TR_Controller (
  input  [20:0] IR,
  input  [15:0] Seq,
  input  R,
  output LD
);

  wire and_1_out, and_2_out, and_3_out, decoder_1_out0, decoder_1_out1, decoder_1_out2, decoder_1_out3,
       decoder_1_out4, decoder_1_out5, decoder_1_out6, decoder_1_out7, decoder_1_out8, decoder_1_out9,
       decoder_1_out10, decoder_1_out11, decoder_1_out12, decoder_1_out13, decoder_1_out14, decoder_1_out15;

  Decoder #(.select(4)) decoder_1 (
    .out0(decoder_1_out0), .out1(decoder_1_out1), .out2(decoder_1_out2), .out3(decoder_1_out3),
    .out4(decoder_1_out4), .out5(decoder_1_out5), .out6(decoder_1_out6), .out7(decoder_1_out7),
    .out8(decoder_1_out8), .out9(decoder_1_out9), .out10(decoder_1_out10), .out11(decoder_1_out11),
    .out12(decoder_1_out12), .out13(decoder_1_out13), .out14(decoder_1_out14), .out15(decoder_1_out15),
    .sel(IR[18:15]));  // open: en
  and and_1 (and_1_out, R, Seq[0]);
  and and_2 (and_2_out, decoder_1_out2, Seq[5]);
  and and_3 (and_3_out, Seq[5], decoder_1_out8);
  or or_1 (LD, and_1_out, and_2_out, and_3_out);
endmodule

module OUTR_Controller (
  input  [20:0] IR,
  input  [15:0] Seq,
  input  I1,
  input  I0,
  input  R,
  output LD
);

  wire decoder_1_out0, decoder_1_out1, decoder_1_out2, decoder_1_out3, decoder_1_out4, decoder_1_out5,
       decoder_1_out6, decoder_1_out7, decoder_1_out8, decoder_1_out9, decoder_1_out10, decoder_1_out11,
       decoder_1_out12, decoder_1_out13, decoder_1_out14, decoder_1_out15, p_out;

  Decoder #(.select(4)) decoder_1 (
    .out0(decoder_1_out0), .out1(decoder_1_out1), .out2(decoder_1_out2), .out3(decoder_1_out3),
    .out4(decoder_1_out4), .out5(decoder_1_out5), .out6(decoder_1_out6), .out7(decoder_1_out7),
    .out8(decoder_1_out8), .out9(decoder_1_out9), .out10(decoder_1_out10), .out11(decoder_1_out11),
    .out12(decoder_1_out12), .out13(decoder_1_out13), .out14(decoder_1_out14), .out15(decoder_1_out15),
    .sel(IR[18:15]));  // open: en
  and p (p_out, decoder_1_out15, I1, I0, Seq[3]);
  and and_1 (LD, p_out, IR[6]);
endmodule

module E_Controller (
  input  [20:0] IR,
  input  [20:0] AC,
  input  [15:0] Seq,
  input  R,
  input  I0,
  input  I1,
  input  in_7,
  input  Cout,
  output Output
);

  wire and_1_out, and_2_out, and_3_out, and_4_out, and_5_out, and_6_out, and_7_out, and_8_out, and_9_out,
       decoder_1_out0, decoder_1_out1, decoder_1_out2, decoder_1_out3, decoder_1_out4, decoder_1_out5,
       decoder_1_out6, decoder_1_out7, decoder_1_out8, decoder_1_out9, decoder_1_out10, decoder_1_out11,
       decoder_1_out12, decoder_1_out13, decoder_1_out14, decoder_1_out15, or_1_out, or_2_out, r_out;

  Decoder #(.select(4)) decoder_1 (
    .out0(decoder_1_out0), .out1(decoder_1_out1), .out2(decoder_1_out2), .out3(decoder_1_out3),
    .out4(decoder_1_out4), .out5(decoder_1_out5), .out6(decoder_1_out6), .out7(decoder_1_out7),
    .out8(decoder_1_out8), .out9(decoder_1_out9), .out10(decoder_1_out10), .out11(decoder_1_out11),
    .out12(decoder_1_out12), .out13(decoder_1_out13), .out14(decoder_1_out14), .out15(decoder_1_out15),
    .sel(IR[18:15]));  // open: en
  and u_r (r_out, decoder_1_out15, ~I0, ~I1, Seq[3]);  // AND_Gate
  and and_1 (and_1_out, decoder_1_out12, Cout, Seq[5]);
  and and_2 (and_2_out, r_out, IR[7], AC[1]);
  and and_3 (and_3_out, r_out, IR[9], AC[20]);
  and and_4 (and_4_out, r_out, IR[5]);
  and and_5 (and_5_out, r_out, IR[4]);
  and and_6 (and_6_out, r_out, IR[11]);
  and and_7 (and_7_out, ~Cout, Seq[5], decoder_1_out12);  // AND_Gate
  and and_8 (and_8_out, r_out, IR[7], ~AC[1]);  // AND_Gate
  and and_9 (and_9_out, r_out, IR[9], ~AC[20]);  // AND_Gate
  or or_1 (or_1_out, and_1_out, and_2_out, and_3_out, and_4_out);
  or or_2 (or_2_out, and_5_out, and_6_out, and_7_out, and_8_out, and_9_out);
  J_K_Flip_Flop j_k_ff_1 (.J(or_1_out), .clk(in_7), .K(or_2_out), .Q(Output));  // open: Qn, preset, en, reset
endmodule

module R_Controller (
  input  [15:0] Seq,
  input  IEN,
  input  FGI,
  input  FGO,
  input  CLK,
  output Output
);

  wire and_1_out, and_2_out, or_1_out;

  or or_1 (or_1_out, FGI, FGO);
  and and_1 (and_1_out, ~Seq[0], ~Seq[1], ~Seq[2], IEN, or_1_out);  // AND_Gate
  and and_2 (and_2_out, Seq[2], Output);
  J_K_Flip_Flop j_k_ff_1 (.J(and_1_out), .clk(CLK), .K(and_2_out), .Q(Output));  // open: Qn, preset, en, reset
endmodule

module S_Controller (
  input  [20:0] IR,
  input  [15:0] Seq,
  input  CLK,
  input  I0,
  input  I1,
  input  R,
  output Output
);

  wire and_1_out, and_2_out, decoder_1_out0, decoder_1_out1, decoder_1_out2, decoder_1_out3, decoder_1_out4,
       decoder_1_out5, decoder_1_out6, decoder_1_out7, decoder_1_out8, decoder_1_out9, decoder_1_out10,
       decoder_1_out11, decoder_1_out12, decoder_1_out13, decoder_1_out14, decoder_1_out15;

  Decoder #(.select(4)) decoder_1 (
    .out0(decoder_1_out0), .out1(decoder_1_out1), .out2(decoder_1_out2), .out3(decoder_1_out3),
    .out4(decoder_1_out4), .out5(decoder_1_out5), .out6(decoder_1_out6), .out7(decoder_1_out7),
    .out8(decoder_1_out8), .out9(decoder_1_out9), .out10(decoder_1_out10), .out11(decoder_1_out11),
    .out12(decoder_1_out12), .out13(decoder_1_out13), .out14(decoder_1_out14), .out15(decoder_1_out15),
    .sel(IR[18:15]));  // open: en
  and and_1 (and_1_out, decoder_1_out15, ~I1, ~I0, Seq[3]);  // AND_Gate
  and and_2 (and_2_out, and_1_out, IR[10]);
  J_K_Flip_Flop j_k_ff_1 (.J(1'b0), .clk(CLK), .K(1'b0), .Qn(Output), .preset(and_2_out));  // open: Q, en, reset
endmodule

module IEN_Controler (
  input  [20:0] IR,
  input  [15:0] Seq,
  input  I0,
  input  I1,
  input  CLK,
  input  R,
  output Output
);

  wire and_1_out, and_2_out, and_3_out, and_4_out, and_5_out, decoder_1_out0, decoder_1_out1, decoder_1_out2,
       decoder_1_out3, decoder_1_out4, decoder_1_out5, decoder_1_out6, decoder_1_out7, decoder_1_out8,
       decoder_1_out9, decoder_1_out10, decoder_1_out11, decoder_1_out12, decoder_1_out13, decoder_1_out14,
       decoder_1_out15, or_1_out;

  Decoder #(.select(4)) decoder_1 (
    .out0(decoder_1_out0), .out1(decoder_1_out1), .out2(decoder_1_out2), .out3(decoder_1_out3),
    .out4(decoder_1_out4), .out5(decoder_1_out5), .out6(decoder_1_out6), .out7(decoder_1_out7),
    .out8(decoder_1_out8), .out9(decoder_1_out9), .out10(decoder_1_out10), .out11(decoder_1_out11),
    .out12(decoder_1_out12), .out13(decoder_1_out13), .out14(decoder_1_out14), .out15(decoder_1_out15),
    .sel(IR[18:15]));  // open: en
  and and_1 (and_1_out, decoder_1_out15, I0, I1, IR[20]);
  and and_2 (and_2_out, decoder_1_out15, I0, I1, IR[20]);
  and and_3 (and_3_out, and_1_out, IR[5]);
  and and_4 (and_4_out, and_2_out, IR[4]);
  and and_5 (and_5_out, R, Seq[2]);
  or or_1 (or_1_out, and_4_out, and_5_out);
  J_K_Flip_Flop j_k_ff_1 (.J(and_3_out), .clk(CLK), .K(or_1_out), .Q(Output));  // open: Qn, preset, en, reset

  assign Seq[3] = IR[20];

  // Other names for the same wires on the sheet: IO = I0
endmodule

module FGI_Controller (
  input  [20:0] IR,
  input  [15:0] Seq,
  input  CLK,
  input  I0,
  input  I1,
  output Output
);

  wire and_1_out, decoder_1_out0, decoder_1_out1, decoder_1_out2, decoder_1_out3, decoder_1_out4,
       decoder_1_out5, decoder_1_out6, decoder_1_out7, decoder_1_out8, decoder_1_out9, decoder_1_out10,
       decoder_1_out11, decoder_1_out12, decoder_1_out13, decoder_1_out14, decoder_1_out15, p_out;

  Decoder #(.select(4)) decoder_1 (
    .out0(decoder_1_out0), .out1(decoder_1_out1), .out2(decoder_1_out2), .out3(decoder_1_out3),
    .out4(decoder_1_out4), .out5(decoder_1_out5), .out6(decoder_1_out6), .out7(decoder_1_out7),
    .out8(decoder_1_out8), .out9(decoder_1_out9), .out10(decoder_1_out10), .out11(decoder_1_out11),
    .out12(decoder_1_out12), .out13(decoder_1_out13), .out14(decoder_1_out14), .out15(decoder_1_out15),
    .sel(IR[18:15]));  // open: en
  and p (p_out, decoder_1_out15, I0, I1, Seq[3]);
  and and_1 (and_1_out, p_out, IR[8]);
  J_K_Flip_Flop j_k_ff_1 (.J(1'b0), .clk(CLK), .K(and_1_out), .Q(Output));  // open: Qn, preset, en, reset
endmodule

module FGO_Controller (
  input  [20:0] IR,
  input  [15:0] Seq,
  input  CLK,
  input  I0,
  input  I1,
  output Output
);

  wire and_1_out, decoder_1_out0, decoder_1_out1, decoder_1_out2, decoder_1_out3, decoder_1_out4,
       decoder_1_out5, decoder_1_out6, decoder_1_out7, decoder_1_out8, decoder_1_out9, decoder_1_out10,
       decoder_1_out11, decoder_1_out12, decoder_1_out13, decoder_1_out14, decoder_1_out15, p_out;

  Decoder #(.select(4)) decoder_1 (
    .out0(decoder_1_out0), .out1(decoder_1_out1), .out2(decoder_1_out2), .out3(decoder_1_out3),
    .out4(decoder_1_out4), .out5(decoder_1_out5), .out6(decoder_1_out6), .out7(decoder_1_out7),
    .out8(decoder_1_out8), .out9(decoder_1_out9), .out10(decoder_1_out10), .out11(decoder_1_out11),
    .out12(decoder_1_out12), .out13(decoder_1_out13), .out14(decoder_1_out14), .out15(decoder_1_out15),
    .sel(IR[18:15]));  // open: en
  and p (p_out, decoder_1_out15, I0, I1, Seq[3]);
  and and_1 (and_1_out, p_out, IR[6]);
  J_K_Flip_Flop j_k_ff_1 (.J(1'b0), .clk(CLK), .K(and_1_out), .Q(Output));  // open: Qn, preset, en, reset
endmodule

module SC_Controller (
  input  [20:0] IR,
  input  [15:0] Seq,
  input  I0,
  input  I1,
  input  R,
  input  S,
  output LD,
  output INC
);

  wire and_1_out, and_2_out, and_3_out, and_4_out, and_5_out, and_6_out, and_7_out, and_8_out, and_9_out,
       and_10_out, and_11_out, and_12_out, and_13_out, and_14_out, and_15_out, and_16_out, decoder_1_out0,
       decoder_1_out1, decoder_1_out2, decoder_1_out3, decoder_1_out4, decoder_1_out5, decoder_1_out6,
       decoder_1_out7, decoder_1_out8, decoder_1_out9, decoder_1_out10, decoder_1_out11, decoder_1_out12,
       decoder_1_out13, decoder_1_out14, decoder_1_out15, or_1_out, p, r_t;

  Decoder #(.select(4)) decoder_1 (
    .out0(decoder_1_out0), .out1(decoder_1_out1), .out2(decoder_1_out2), .out3(decoder_1_out3),
    .out4(decoder_1_out4), .out5(decoder_1_out5), .out6(decoder_1_out6), .out7(decoder_1_out7),
    .out8(decoder_1_out8), .out9(decoder_1_out9), .out10(decoder_1_out10), .out11(decoder_1_out11),
    .out12(decoder_1_out12), .out13(decoder_1_out13), .out14(decoder_1_out14), .out15(decoder_1_out15),
    .sel(IR[18:15]));  // open: en
  and u_r (r_t, decoder_1_out15, ~I1, ~I0, IR[20]);  // AND_Gate
  and u_p (p, decoder_1_out15, I1, I0, IR[20]);
  and and_1 (and_1_out, R, Seq[2]);
  and and_2 (and_2_out, decoder_1_out0, Seq[5]);
  and and_3 (and_3_out, decoder_1_out1, Seq[5]);
  and and_4 (and_4_out, decoder_1_out4, Seq[5]);
  and and_5 (and_5_out, decoder_1_out6, Seq[5]);
  and and_6 (and_6_out, decoder_1_out7, Seq[5]);
  and and_7 (and_7_out, decoder_1_out9, Seq[5]);
  and and_8 (and_8_out, decoder_1_out10, Seq[5]);
  and and_9 (and_9_out, decoder_1_out11, Seq[5]);
  and and_10 (and_10_out, decoder_1_out12, Seq[5]);
  and and_11 (and_11_out, decoder_1_out14, Seq[5]);
  and and_12 (and_12_out, decoder_1_out2, Seq[6]);
  and and_13 (and_13_out, decoder_1_out13, Seq[6]);
  and and_14 (and_14_out, decoder_1_out10, Seq[6]);
  and and_15 (and_15_out, decoder_1_out12, Seq[6]);
  and and_16 (and_16_out, decoder_1_out8, Seq[7]);
  or or_1 (or_1_out, r_t, p, and_1_out, and_2_out, and_3_out, and_4_out, and_5_out, and_6_out, and_7_out, and_8_out, and_9_out, and_10_out, and_11_out, and_12_out, and_13_out, and_14_out, and_15_out, and_16_out);
  and and_17 (LD, or_1_out, S);
  and and_18 (INC, ~or_1_out, S);  // AND_Gate

  assign Seq[3] = IR[20];
endmodule

module SC (
  input  Clear,
  input  Load,
  input  INC,
  input  CLK,
  output A,
  output A_2,
  output A_3,
  output A_4,
  output A_5,
  output A_6,
  output A_7,
  output A_8,
  output C_out
);

  wire and_1_out, and_2_out, and_3_out, and_4_out, and_5_out, and_6_out, and_7_out, and_8_out, and_9_out,
       and_10_out, and_11_out, and_12_out, and_13_out, and_14_out, and_15_out, and_16_out, and_18_out,
       and_19_out, and_21_out, and_22_out, and_24_out, and_25_out, or_1_out, or_2_out, or_3_out, or_4_out,
       or_5_out, or_6_out, or_7_out, or_8_out, or_9_out, or_10_out, or_11_out, or_12_out, or_13_out,
       or_14_out, or_15_out, or_16_out, undriven, undriven_2, undriven_3, undriven_4, undriven_5, undriven_6,
       undriven_7, undriven_8;

  and and_1 (and_1_out, ~Clear, Load);  // AND_Gate
  and and_2 (and_2_out, ~Clear, ~Load, INC);  // AND_Gate
  and and_3 (and_3_out, and_1_out, undriven);
  and and_4 (and_4_out, and_1_out, ~undriven);  // AND_Gate
  and and_5 (and_5_out, and_2_out, A);
  and and_6 (and_6_out, and_1_out, undriven_2);
  and and_7 (and_7_out, and_1_out, ~undriven_2);  // AND_Gate
  and and_8 (and_8_out, and_5_out, A_2);
  and and_9 (and_9_out, and_1_out, undriven_3);
  and and_10 (and_10_out, and_1_out, ~undriven_3);  // AND_Gate
  and and_11 (and_11_out, and_8_out, A_3);
  and and_12 (and_12_out, and_1_out, undriven_4);
  and and_13 (and_13_out, and_1_out, ~undriven_4);  // AND_Gate
  and and_14 (and_14_out, and_11_out, A_4);
  and and_15 (and_15_out, and_1_out, undriven_5);
  and and_16 (and_16_out, and_1_out, ~undriven_5);  // AND_Gate
  and and_17 (Clear, and_14_out, A_5);
  and and_18 (and_18_out, and_1_out, undriven_6);
  and and_19 (and_19_out, and_1_out, ~undriven_6);  // AND_Gate
  and and_20 (Clear, Clear, A_6);
  and and_21 (and_21_out, and_1_out, undriven_7);
  and and_22 (and_22_out, and_1_out, ~undriven_7);  // AND_Gate
  and and_23 (Clear, Clear, A_7);
  and and_24 (and_24_out, and_1_out, undriven_8);
  and and_25 (and_25_out, and_1_out, ~undriven_8);  // AND_Gate
  and and_26 (C_out, Clear, A_8);
  or or_1 (or_1_out, and_2_out, and_3_out);
  or or_2 (or_2_out, Clear, and_2_out, and_4_out);
  or or_3 (or_3_out, and_5_out, and_6_out);
  or or_4 (or_4_out, Clear, and_5_out, and_7_out);
  or or_5 (or_5_out, and_8_out, and_9_out);
  or or_6 (or_6_out, Clear, and_8_out, and_10_out);
  or or_7 (or_7_out, and_11_out, and_12_out);
  or or_8 (or_8_out, Clear, and_11_out, and_13_out);
  or or_9 (or_9_out, and_14_out, and_15_out);
  or or_10 (or_10_out, Clear, and_14_out, and_16_out);
  or or_11 (or_11_out, Clear, and_18_out);
  or or_12 (or_12_out, Clear, Clear, and_19_out);
  or or_13 (or_13_out, Clear, and_21_out);
  or or_14 (or_14_out, Clear, Clear, and_22_out);
  or or_15 (or_15_out, Clear, and_24_out);
  or or_16 (or_16_out, Clear, Clear, and_25_out);
  J_K_Flip_Flop j_k_ff_1 (.J(or_1_out), .clk(CLK), .K(or_2_out), .Q(A));  // open: Qn, preset, en, reset
  J_K_Flip_Flop j_k_ff_2 (.J(or_3_out), .clk(CLK), .K(or_4_out), .Q(A_2));  // open: Qn, preset, en, reset
  J_K_Flip_Flop j_k_ff_3 (.J(or_5_out), .clk(CLK), .K(or_6_out), .Q(A_3));  // open: Qn, preset, en, reset
  J_K_Flip_Flop j_k_ff_4 (.J(or_7_out), .clk(CLK), .K(or_8_out), .Q(A_4));  // open: Qn, preset, en, reset
  J_K_Flip_Flop j_k_ff_5 (.J(or_9_out), .clk(CLK), .K(or_10_out), .Q(A_5));  // open: Qn, preset, en, reset
  J_K_Flip_Flop j_k_ff_6 (.J(or_11_out), .clk(CLK), .K(or_12_out), .Q(A_6));  // open: Qn, preset, en, reset
  J_K_Flip_Flop j_k_ff_7 (.J(or_13_out), .clk(CLK), .K(or_14_out), .Q(A_7));  // open: Qn, preset, en, reset
  J_K_Flip_Flop j_k_ff_8 (.J(or_15_out), .clk(CLK), .K(or_16_out), .Q(A_8));  // open: Qn, preset, en, reset
endmodule

module I1_Controller (
  input  [20:0] IR,
  input  [15:0] Seq,
  input  R,
  input  CLK,
  output out_5
);

  wire and_1_out, and_2_out;

  and and_1 (and_1_out, Seq[2], IR[19], ~R);  // AND_Gate
  and and_2 (and_2_out, ~R, Seq[2], ~IR[19]);  // AND_Gate
  J_K_Flip_Flop j_k_ff_1 (.J(and_1_out), .clk(CLK), .K(and_2_out), .Q(out_5));  // open: Qn, preset, en, reset
endmodule

module I0_Controller (
  input  [20:0] IR,
  input  [15:0] Seq,
  input  R,
  input  CLK,
  output out_5
);

  wire and_1_out, and_2_out;

  and and_1 (and_1_out, Seq[2], IR[20], ~R);  // AND_Gate
  and and_2 (and_2_out, ~R, Seq[2], ~IR[20]);  // AND_Gate
  J_K_Flip_Flop j_k_ff_1 (.J(and_1_out), .clk(CLK), .K(and_2_out), .Q(out_5));  // open: Qn, preset, en, reset
endmodule

module ALU_Controller (
  input  [20:0] IR,
  input  [15:0] Seq,
  input  I0,
  input  I1,
  output [3:0] out_5
);

  wire ADD_out, AND_2_out, COM_out, DEC_out, decoder_1_out0, decoder_1_out1, decoder_1_out2, decoder_1_out3,
       decoder_1_out4, decoder_1_out5, decoder_1_out6, decoder_1_out7, decoder_1_out8, decoder_1_out9,
       decoder_1_out10, decoder_1_out11, decoder_1_out12, decoder_1_out13, decoder_1_out14, decoder_1_out15,
       DR_2_out, DR_out, INPR_out, NAND_out, NOR_out, not_1_out, or_2_out, or_3_out, or_4_out, OR_out, p_out,
       r, SHL_out, SHR_out, SUB_out, TR_out, XOR_2_out, XOR_out;

  Decoder #(.select(4)) decoder_1 (
    .out0(decoder_1_out0), .out1(decoder_1_out1), .out2(decoder_1_out2), .out3(decoder_1_out3),
    .out4(decoder_1_out4), .out5(decoder_1_out5), .out6(decoder_1_out6), .out7(decoder_1_out7),
    .out8(decoder_1_out8), .out9(decoder_1_out9), .out10(decoder_1_out10), .out11(decoder_1_out11),
    .out12(decoder_1_out12), .out13(decoder_1_out13), .out14(decoder_1_out14), .out15(decoder_1_out15),
    .sel(IR[18:15]));  // open: en
  and ADD (ADD_out, decoder_1_out12, Seq[5]);
  and and_1 (r, decoder_1_out15, ~I1, ~I0, Seq[3]);  // AND_Gate
  and AND_2 (AND_2_out, decoder_1_out0, Seq[5]);
  and DR (DR_out, decoder_1_out8, Seq[6]);
  and DR_2 (DR_2_out, decoder_1_out11, Seq[5]);
  and p (p_out, decoder_1_out15, I0, I1, Seq[3]);
  and INPR (INPR_out, p_out, IR[12]);
  and COM (COM_out, r, IR[6]);
  and SHR (SHR_out, r, IR[7]);
  and SHL (SHL_out, r, IR[9]);
  and OR (OR_out, decoder_1_out0, Seq[5]);
  and XOR (XOR_out, decoder_1_out2, Seq[5]);
  and XOR_2 (XOR_2_out, decoder_1_out6, Seq[5]);
  and NAND (NAND_out, decoder_1_out10, Seq[5]);
  and NOR (NOR_out, decoder_1_out9, Seq[5]);
  and SUB (SUB_out, decoder_1_out14, Seq[5]);
  and TR (TR_out, decoder_1_out2, Seq[6]);
  and DEC (DEC_out, r, IR[3]);
  or or_2 (or_2_out, DR_out, DR_2_out);
  or or_3 (or_3_out, XOR_out, XOR_2_out);
  not not_1 (not_1_out, or_4_out);
  or or_4 (or_4_out, AND_2_out, ADD_out, or_2_out, INPR_out, COM_out, SHR_out, SHL_out, OR_out, or_3_out, NAND_out, NOR_out, SUB_out, TR_out, DEC_out);
  Priority_Encoder #(.select(4)) priority_encoder_1 (
    .in0(not_1_out), .in1(AND_2_out), .in2(ADD_out), .in3(or_2_out), .in4(INPR_out), .in5(COM_out),
    .in6(SHR_out), .in7(SHL_out), .in8(OR_out), .in9(or_3_out), .in10(NAND_out), .in11(NOR_out),
    .in12(SUB_out), .in13(TR_out), .in14(DEC_out), .in15(1'b0), .out(out_5));  // open: gs, en_out, en_in
endmodule

module ALU (
  input  [15:0] Seq,
  input  [20:0] IR,
  input  [20:0] AC,
  input  [20:0] DR,
  input  Carry_in,
  input  I0,
  input  I1,
  input  [7:0] INPR,
  input  [20:0] TR,
  output C_out,
  output [20:0] AC_input
);

  wire [3:0] alu_controller_1_out_5;
  wire [20:0] adder_1_out, adder_2_out, adder_3_out, adder_4_out, and_1_out, and_2_out, and_3_out, and_4_out,
       and_5_out, and_6_out, and_7_out, and_8_out, and_9_out, and_10_out, and_11_out, and_12_out, and_13_out,
       and_14_out, and_15_out, demultiplexer_1_out0, demultiplexer_1_out1, demultiplexer_1_out2,
       demultiplexer_1_out3, demultiplexer_1_out4, demultiplexer_1_out5, demultiplexer_1_out6,
       demultiplexer_1_out7, demultiplexer_1_out8, demultiplexer_1_out9, demultiplexer_1_out10,
       demultiplexer_1_out11, demultiplexer_1_out12, demultiplexer_1_out13, demultiplexer_1_out14,
       nand_1_out, nor_1_out, not_1_out, or_1_out, shifter_1_out, shifter_2_out, xor_1_out;

  ALU_Controller alu_controller_1 (.IR(IR), .I0(I0), .I1(I1), .Seq(Seq), .out_5(alu_controller_1_out_5));
  Demultiplexer #(.select(4), .width(21), .enable("false")) demultiplexer_1 (
    .out0(demultiplexer_1_out0), .out1(demultiplexer_1_out1), .out2(demultiplexer_1_out2),
    .out3(demultiplexer_1_out3), .out4(demultiplexer_1_out4), .out5(demultiplexer_1_out5),
    .out6(demultiplexer_1_out6), .out7(demultiplexer_1_out7), .out8(demultiplexer_1_out8),
    .out9(demultiplexer_1_out9), .out10(demultiplexer_1_out10), .out11(demultiplexer_1_out11),
    .out12(demultiplexer_1_out12), .out13(demultiplexer_1_out13), .out14(demultiplexer_1_out14),
    .in({21{1'b1}}), .sel(alu_controller_1_out_5));  // open: out15
  Shifter #(.width(21), .shift("rr")) shifter_1 (.in(AC), .\dist (5'b00001), .out(shifter_1_out));
  Shifter #(.width(21), .shift("rl")) shifter_2 (.in(AC), .\dist (5'b00001), .out(shifter_2_out));
  assign not_1_out = ~DR;  // NOT_Gate not_1, 21 bits wide
  assign and_1_out = AC & demultiplexer_1_out0;  // AND_Gate and_1, 21 bits wide
  Adder #(.width(21)) adder_1 (.a(21'h1), .b(not_1_out), .out(adder_1_out));  // open: cin, cout
  Adder #(.width(21)) adder_2 (.a(DR), .b(AC), .out(adder_2_out), .cin(Carry_in), .cout(C_out));
  assign or_1_out = AC | DR;  // OR_Gate or_1, 21 bits wide
  assign xor_1_out = AC ^ DR;  // XOR_Gate xor_1, 21 bits wide
  assign nand_1_out = ~(DR & DR);  // NAND_Gate nand_1, 21 bits wide
  assign nor_1_out = ~(AC | DR);  // NOR_Gate nor_1, 21 bits wide
  Adder #(.width(21)) adder_3 (.a(AC), .b(adder_1_out), .out(adder_3_out));  // open: cin, cout
  Adder #(.width(21)) adder_4 (.a({21{1'b1}}), .b(AC), .out(adder_4_out));  // open: cin, cout
  assign and_2_out = demultiplexer_1_out1 & AC & DR;  // AND_Gate and_2, 21 bits wide
  assign and_3_out = demultiplexer_1_out2 & adder_2_out;  // AND_Gate and_3, 21 bits wide
  assign and_4_out = demultiplexer_1_out3 & DR;  // AND_Gate and_4, 21 bits wide
  assign and_5_out = demultiplexer_1_out4 & {{13{1'b0}}, INPR};  // AND_Gate and_5, 21 bits wide
  assign and_6_out = demultiplexer_1_out5 & ~AC;  // AND_Gate and_6, 21 bits wide
  assign and_7_out = demultiplexer_1_out6 & shifter_1_out;  // AND_Gate and_7, 21 bits wide
  assign and_8_out = demultiplexer_1_out7 & shifter_2_out;  // AND_Gate and_8, 21 bits wide
  assign and_9_out = demultiplexer_1_out8 & or_1_out;  // AND_Gate and_9, 21 bits wide
  assign and_10_out = demultiplexer_1_out9 & xor_1_out;  // AND_Gate and_10, 21 bits wide
  assign and_11_out = demultiplexer_1_out10 & nand_1_out;  // AND_Gate and_11, 21 bits wide
  assign and_12_out = demultiplexer_1_out11 & nor_1_out;  // AND_Gate and_12, 21 bits wide
  assign and_13_out = demultiplexer_1_out12 & adder_3_out;  // AND_Gate and_13, 21 bits wide
  assign and_14_out = demultiplexer_1_out13 & TR;  // AND_Gate and_14, 21 bits wide
  assign and_15_out = demultiplexer_1_out14 & adder_4_out;  // AND_Gate and_15, 21 bits wide
  assign AC_input = and_1_out | and_2_out | and_3_out | and_4_out | and_5_out | and_6_out | and_7_out | and_8_out | and_9_out | and_10_out | and_11_out | and_12_out | and_13_out | and_14_out | and_15_out;  // OR_Gate or_2, 21 bits wide

  // Other names for the same wires on the sheet: INPR_t[7:0] = INPR

  // Notes on the sheet:
  //   Right Shifter
  //   Left shifter
endmodule
